# Fritzing sketch dc_motor_l298_H_bridge (saved by Fritzing 0.9.3b)

parts:
  Part1 = Arduino Uno (Rev3)
  VCC1 = Battery
  Part3 = Arduino Motor Shield  # not connected
  M1 = DC Motor  # not connected

nets:
  N1: Part1.GND, VCC1.-
