# Fritzing sketch hc_sr04 (saved by Fritzing 0.9.3b)

parts:
  Part1 = Arduino Uno (Rev3)
  hc-sr1 = hc-sr04

nets:
  N1: Part1.D10_PWM/SS, hc-sr1.Trig
  N2: Part1.D13/SCK, hc-sr1.Echo
  5V: Part1.5V, hc-sr1.VCC
  GND: Part1.GND, hc-sr1.GND

notes:
  5V - VCC
  10 - TRIG
  13 - ECHO
  GND - GND
